# Fritzing sketch niku-rp2 (saved by Fritzing 0.9.2b)
breadboards: 1

parts:
  Raspberry_Pi2 = Raspberry Pi 2
  R1 = Resistor [tolerance=±5% resistance=4.7k package=THT]
  Solid_State_Relay = RELAY-SOLIDSTATE [package=relay-s108t02]
  DS1 = DS18B20 1-Wire Temperature Sensor [part_number=DS18B20]
  R2 = Resistor [tolerance=±5% resistance=10k package=THT]
  R3 = Resistor [tolerance=±5% resistance=100 package=THT]
  Q1 = NPN-Transistor [package="TO92 [THT]"]

nets:
  3V3: Raspberry_Pi2.3v3, R1.Pin_0, DS1.VDD
  GND: Raspberry_Pi2.GND, DS1.GND, R3.Pin_0, Q1.E
  N1: Raspberry_Pi2.GPIO21, R2.Pin_1
  N2: Raspberry_Pi2.GPIO20, R1.Pin_1, DS1.DQ
  N3: Raspberry_Pi2.5V, Solid_State_Relay.+
  N4: Solid_State_Relay.-, Q1.C
  N5: R2.Pin_0, R3.Pin_1, Q1.B

notes:
  DS18B20
  100V POT
  Raspberrry Pi2
